# Fritzing sketch Wiring plan (saved by Fritzing 0.9.4)
stripboards: 2

parts:
  WeMos_D1_Mini1 = WeMos D1 Mini  # not connected
  U1 = PCF8574 [package="DIP16 [THT]"]  # not connected
  JP1 = Header 1 [package=1x01_offset]
  JP2 = Header 1 [package=1x01_offset]
  JP3 = Header 1 [package=1x01_offset]
  JP4 = Header 1 [package=1x01_offset]
  JP7 = Header 1 [package=1x01_offset]  # not connected
  JP8 = Header 1 [package=1x01_offset]
  JP9 = Header 1 [package=1x01_offset]  # not connected
  JP10 = Header 1 [package=1x01_offset]  # not connected
  JP11 = Header 1 [package=1x01_offset]
  JP12 = Header 1 [package=1x01_offset]
  JP13 = Header 1 [package=1x01_offset]
  JP14 = Header 1 [package=1x01_offset]  # not connected
  JP5 = Header 1 [package=1x01_offset]
  JP15 = Header 1 [package=1x01_offset]
  JP16 = Header 1 [package=1x01_offset]
  JP17 = Header 1 [package=1x01_offset]
  JP18 = Header 1 [package=1x01_offset]  # not connected
  JP19 = Header 1 [package=1x01_offset]
  JP20 = Header 1 [package=1x01_offset]
  JP21 = Header 1 [package=1x01_offset]
  JP22 = Header 1 [package=1x01_offset]  # not connected
  JP23 = Header 1 [package=1x01_offset]  # not connected
  JP24 = Header 1 [package=1x01_offset]  # not connected
  JP25 = Header 1 [package=1x01_offset]
  JP26 = Header 1 [package=1x01_offset]
  JP27 = Header 1 [package=1x01_offset]  # not connected
  JP28 = Header 1 [package=1x01_offset]  # not connected
  JP29 = Header 1 [package=1x01_offset]
  JP30 = Header 1 [package=1x01_offset]
  JP31 = Header 1 [package=1x01_offset]
  JP32 = Header 1 [package=1x01_offset]
  JP36 = Header 1 [package=1x01_offset]
  JP37 = Header 1 [package=1x01_offset]
  JP38 = Header 1 [package=1x01_offset]
  JP39 = Header 1 [package=1x01_offset]
  JP40 = Header 1 [package=1x01_offset]
  JP41 = Header 1 [package=1x01_offset]
  JP42 = Header 1 [package=1x01_offset]
  JP43 = Header 1 [package=1x01_offset]
  R1 = Resistor [tolerance=±5% resistance=4.7k package="0402 [SMD]"]  # not connected
  R2 = Resistor [tolerance=±5% resistance=4.7k package="0402 [SMD]"]  # not connected
  R3 = Resistor [tolerance=±5% resistance=10k package="0402 [SMD]"]
  JP44 = Header 1 [package=1x01_offset]  # not connected
  JP45 = Header 1 [package=1x01_offset]  # not connected
  JP46 = Header 1 [package=1x01_offset]  # not connected
  JP47 = Header 1 [package=1x01_offset]  # not connected
  JP48 = Header 1 [package=1x01_offset]  # not connected
  JP49 = Header 1 [package=1x01_offset]
  JP50 = Header 1 [package=1x01_offset]
  JP51 = Header 1 [package=1x01_offset]
  JP52 = Header 1 [package=1x01_offset]
  JP53 = Header 1 [package=1x01_offset]
  JP54 = Header 1 [package=1x01_offset]  # not connected
  JP55 = Header 1 [package=1x01_offset]  # not connected
  JP56 = Header 1 [package=1x01_offset]
  JP57 = Header 1 [package=1x01_offset]
  JP58 = Header 1 [package=1x01_offset]
  JP59 = Header 1 [package=1x01_offset]
  JP60 = Header 1 [package=1x01_offset]

nets:
  N1: JP1.1, JP2.1, JP3.1, JP4.1, JP15.1, JP16.1
  N2: JP8.1, JP5.1
  N3: JP11.1, JP19.1
  N4: JP12.1, JP21.1
  N5: JP13.1, JP17.1, JP20.1
  N6: JP25.1, JP39.1, JP43.1, JP57.1
  N7: JP26.1, JP32.1, JP40.1, JP42.1, R3.Pin_0, JP49.1, JP53.1
  N8: JP29.1, JP38.1, JP51.1
  N9: JP30.1, JP56.1
  N10: JP31.1, JP37.1
  N11: JP36.1, JP52.1
  N12: JP41.1, JP59.1
  N13: R3.Pin_1, JP50.1
  N14: JP58.1, JP60.1
